# Fritzing sketch K2000 (saved by Fritzing 0.3.19b)
breadboards: 1

parts:
  Arduino1 = Arduino
  U1 = 74HC595 [package="DIP16 [THT]"]
  LED1 = Red LED - 5mm
  LED2 = Red LED - 5mm
  LED3 = Red LED - 5mm
  LED4 = Red LED - 5mm
  LED5 = Red LED - 5mm
  LED6 = Red LED - 5mm
  LED7 = Red LED - 5mm
  LED8 = Red LED - 5mm
  R1 = Resistor [resistance=220 package=THT]
  R1_2 = Resistor [resistance=220 package=THT]
  R1_3 = Resistor [resistance=220 package=THT]
  R1_4 = Resistor [resistance=220 package=THT]
  R1_5 = Resistor [resistance=220 package=THT]
  R1_6 = Resistor [resistance=220 package=THT]
  R1_7 = Resistor [resistance=220 package=THT]
  R1_8 = Resistor [resistance=220 package=THT]

nets:
  GND: Arduino1.GND, U1.GND, U1.OE, LED1.connector0, LED2.connector0, LED3.connector0, LED4.connector0, LED5.connector0, LED6.connector0, LED7.connector0, LED8.connector0
  N1: Arduino1.D13, U1.DS
  N2: Arduino1.D12, U1.ST_CP
  N3: Arduino1.D8, U1.SH_CP
  +5V: Arduino1.+5V, U1.MR, U1.VCC
  N4: U1.Q1, R1_2.Pin_1
  N5: U1.Q2, R1_3.Pin_1
  N6: U1.Q3, R1_4.Pin_1
  N7: U1.Q4, R1_5.Pin_1
  N8: U1.Q5, R1_6.Pin_1
  N9: U1.Q6, R1_7.Pin_1
  N10: U1.Q7, R1_8.Pin_1
  N11: U1.Q0, R1.Pin_1
  N12: LED1.connector1, R1_4.Pin_0
  N13: LED2.connector1, R1_3.Pin_0
  N14: LED3.connector1, R1.Pin_0
  N15: LED4.connector1, R1_2.Pin_0
  N16: LED5.connector1, R1_5.Pin_0
  N17: LED6.connector1, R1_6.Pin_0
  N18: LED7.connector1, R1_7.Pin_0
  N19: LED8.connector1, R1_8.Pin_0
