# Fritzing sketch canonIR (saved by Fritzing 0.4.3b)
breadboards: 1

parts:
  Arduino1 = Arduino
  R1 = Resistor [resistance=220 package=THT]
  LED1 = Blue LED - 5mm

nets:
  N1: Arduino1.D12, LED1.cathode
  N2: Arduino1.GND, R1.Pin_1
  N3: R1.Pin_0, LED1.anode
