# Fritzing sketch led-wall (saved by Fritzing 0.3.19b)
breadboards: 1

parts:
  LED3 = Red LED - 5mm
  LED4 = Red LED - 5mm
  LED5 = Red LED - 5mm
  LED3_2 = Red LED - 5mm
  LED4_2 = Red LED - 5mm
  LED5_2 = Red LED - 5mm
  LED3_3 = Red LED - 5mm
  LED4_3 = Red LED - 5mm
  LED5_3 = Red LED - 5mm
  Arduino1 = Arduino

nets:
  N1: LED3.cathode, LED3_2.cathode, LED3_3.cathode, Arduino1.D11
  N2: LED3.anode, LED4.anode, LED5.anode, Arduino1.D10
  N3: LED4.cathode, LED4_2.cathode, LED4_3.cathode, Arduino1.D12
  N4: LED5.cathode, LED5_2.cathode, LED5_3.cathode, Arduino1.D13
  N5: LED3_2.anode, LED4_2.anode, LED5_2.anode, Arduino1.D9
  N6: LED3_3.anode, LED4_3.anode, LED5_3.anode, Arduino1.D8
