# Fritzing sketch ledmatrix_8x8 (saved by Fritzing 0.3.19b)
breadboards: 1

parts:
  Arduino1 = Arduino
  U1 = 74HC595 [package="DIP16 [THT]"]
  BS1 = BASIC Stamp 2 sx
  U2 = 74HC595 [package="DIP16 [THT]"]

nets:
  GND: Arduino1.GND, U1.Q4, U1.Q5, U1.GND, U2.GND, U2.OE
  N1: Arduino1.D13, U2.DS
  N2: Arduino1.D12, U2.ST_CP
  N3: Arduino1.D8, U2.SH_CP
  N4: Arduino1.D5, U1.Q1
  N5: Arduino1.D4, U1.Q2
  N6: Arduino1.D3, U1.Q3
  N7: Arduino1.D2, U1.Q6
  VCC: Arduino1.+5V, U1.VCC, U2.MR, U2.VCC
  N8: U1.Q7, BS1.P7
  N9: U1.Q7', BS1.P4
  N10: U1.MR, BS1.P1
  N11: U1.SH_CP, BS1.ATN
  N12: U1.ST_CP, BS1.P8
  N13: U1.OE, BS1.P11
  N14: U1.DS, BS1.P14
  N15: U1.Q0, BS1.RES
  N16: BS1.SOUT, U2.Q4
  N17: BS1.VSS, U2.Q5
  N18: BS1.P2, U2.Q6
  N19: BS1.P5, U2.Q7
  N20: BS1.P10, U2.Q3
  N21: BS1.P13, U2.Q2
  N22: BS1.VDD, U2.Q1
  N23: BS1.VIN, U2.Q0
