# Fritzing sketch schema_fritzing (saved by Fritzing 0.3.19b)

parts:
  Arduino1 = Arduino
  LED1 = Red LED - 5mm
  R1 = Rotary Potentiometer (Large) [package=THT]

nets:
  N1: Arduino1.GND, LED1.cathode, R1.leg2
  N2: Arduino1.D3, LED1.anode
  N3: Arduino1.+5V, R1.leg1
  N4: Arduino1.A1, R1.wiper
